// Logisim project 120772_1_zad.circ as structural Verilog: 1 circuit, main circuit main
module main (
  input  A,
  input  B,
  input  C,
  input  D,
  output Y_zad,
  output Z_zad,
  output Y_DNF,
  output Z_DNF,
  output Y_KNF,
  output Z_KNF
);

  wire A_B_out, A_C_out, A_nD_out, B_C_out, B_D_out, B_nD_out, C_D_out, C_nD_out, n_A_B_out, n_B_D_out,
       n_C_nD_out, not_1_out, not_2_out, not_3_out;

  not not_1 (not_1_out, D);
  not not_2 (not_2_out, D);
  not not_3 (not_3_out, D);
  nand n_A_B (n_A_B_out, A, B);
  nand n_C_nD (n_C_nD_out, C, not_1_out);
  nand n_B_D (n_B_D_out, B, D);
  and A_B (A_B_out, A, B);
  and C_nD (C_nD_out, C, not_2_out);
  and B_D (B_D_out, B, D);
  or A_C (A_C_out, A, C);
  or A_nD (A_nD_out, A, not_3_out);
  or B_C (B_C_out, B, C);
  or B_nD (B_nD_out, B, not_3_out);
  or C_D (C_D_out, C, D);
  nand n_n_A_B__n_C_nD (Y_zad, n_A_B_out, n_C_nD_out);
  nand n_nC_nD__n_B_D (Z_zad, n_C_nD_out, n_B_D_out);
  or A_B_C_nD (Y_DNF, A_B_out, C_nD_out);
  or C_nD_B_D (Z_DNF, C_nD_out, B_D_out);
  and A_C___B_C___A_nD___B_nD (Y_KNF, A_C_out, A_nD_out, B_C_out, B_nD_out);
  and B_C___B_nD___C_D (Z_KNF, B_nD_out, B_C_out, C_D_out);
endmodule
