// Logisim project ZADANIE_3.circ as structural Verilog: 1 circuit, main circuit main
module main (
  input  X,
  input  rst,
  output Y
);

  wire clc_out, j_k_ff_1_q, j_k_ff_1_qn, j_k_ff_2_q, j_k_ff_2_qn, j_k_ff_3_q, j_k_ff_3_qn, nand_1_out,
       nand_2_out, nand_3_out, nand_4_out, nand_5_out, nand_6_out, nand_7_out, nand_8_out, nand_9_out,
       nand_10_out, nand_11_out, nand_12_out, nand_13_out, nand_14_out, nand_15_out, nand_16_out,
       nand_17_out, nand_19_out, nX_out;

  nand nX (nX_out, X, X);
  Clock clc (.out(clc_out));
  nand nand_1 (nand_1_out, j_k_ff_2_q, X, j_k_ff_3_q);
  nand nand_2 (nand_2_out, X, j_k_ff_2_qn, j_k_ff_3_qn);
  nand nand_3 (nand_3_out, j_k_ff_2_q, nX_out);
  nand nand_4 (nand_4_out, j_k_ff_3_q, nX_out);
  nand nand_5 (nand_5_out, nX_out, j_k_ff_1_qn, j_k_ff_3_q);
  nand nand_6 (nand_6_out, X, j_k_ff_1_q, j_k_ff_3_q);
  nand nand_7 (nand_7_out, X, j_k_ff_1_qn);
  nand nand_8 (nand_8_out, j_k_ff_1_q, j_k_ff_2_qn);
  nand nand_9 (nand_9_out, X, j_k_ff_1_qn, j_k_ff_2_qn);
  nand nand_10 (nand_10_out, j_k_ff_1_q, X, j_k_ff_2_q);
  nand nand_11 (nand_11_out, nX_out, j_k_ff_1_qn, j_k_ff_3_qn);
  nand nand_12 (nand_12_out, X, j_k_ff_1_q);
  nand nand_13 (nand_13_out, X, j_k_ff_3_q);
  nand nand_14 (nand_14_out, nand_1_out, nand_1_out);
  nand nand_15 (nand_15_out, nand_2_out, nand_3_out, nand_4_out);
  nand nand_16 (nand_16_out, nand_5_out, nand_6_out);
  nand nand_17 (nand_17_out, nand_7_out, nand_8_out);
  nand nand_18 (Y, nand_10_out, nand_10_out);
  nand nand_19 (nand_19_out, nand_11_out, nand_12_out, nand_13_out);
  J_K_Flip_Flop j_k_ff_1 (
    .J(nand_14_out), .clk(clc_out), .K(nand_15_out), .Q(j_k_ff_1_q), .Qn(j_k_ff_1_qn), .reset(rst));  // open: preset, en
  J_K_Flip_Flop j_k_ff_2 (
    .J(nand_16_out), .clk(clc_out), .K(nand_19_out), .Q(j_k_ff_2_q), .Qn(j_k_ff_2_qn), .reset(rst));  // open: preset, en
  J_K_Flip_Flop j_k_ff_3 (
    .J(nand_17_out), .clk(clc_out), .K(nand_9_out), .Q(j_k_ff_3_q), .Qn(j_k_ff_3_qn), .reset(rst));  // open: preset, en
endmodule
